// Logisim project logisim.circ as structural Verilog: 7 circuits, main circuit project_ao
module project_ao (
  input  [15:0] A,
  input  [15:0] B,
  input  [3:0] auSEL,
  output [15:0] auRESULT
);

  wire [15:0] adder_1_out, and_1_out, divider_1_out, divider_1_rem, multiplier_1_out, negator_1_out,
       negator_2_out, or_1_out, shifter_1_out, shifter_2_out, shifter_3_out, shifter_4_out, subtractor_1_out,
       xor_1_out;

  Adder #(.width(16)) adder_1 (.a(A), .b(B), .out(adder_1_out));  // open: cin, cout
  Subtractor #(.width(16)) subtractor_1 (.a(A), .b(B), .out(subtractor_1_out));  // open: bin, bout
  assign and_1_out = A & B;  // AND_Gate and_1, 16 bits wide
  assign or_1_out = A | B;  // OR_Gate or_1, 16 bits wide
  assign xor_1_out = A ^ B;  // XOR_Gate xor_1, 16 bits wide
  Divider #(.width(16)) divider_1 (.a(A), .b(B), .out(divider_1_out), .rem(divider_1_rem));  // open: upper
  Multiplier #(.width(16)) multiplier_1 (.a(A), .b(B), .out(multiplier_1_out));  // open: cin, cout
  Shifter #(.width(16)) shifter_1 (.in(A), .\dist (4'b0010), .out(shifter_1_out));
  Shifter #(.width(16)) shifter_2 (.in(B), .\dist (4'b0010), .out(shifter_2_out));
  Shifter #(.shift("lr"), .width(16)) shifter_3 (.in(A), .\dist (4'b0010), .out(shifter_3_out));
  Shifter #(.shift("lr"), .width(16)) shifter_4 (.in(B), .\dist (4'b0010), .out(shifter_4_out));
  Negator #(.width(16)) negator_1 (.in(A), .out(negator_1_out));
  Negator #(.width(16)) negator_2 (.in(B), .out(negator_2_out));
  Multiplexer #(.select(4), .width(16)) multiplexer_1 (
    .in0(adder_1_out), .in1(subtractor_1_out), .in2(and_1_out), .in3(or_1_out), .in4(xor_1_out),
    .in5(divider_1_out), .in6(divider_1_rem), .in7(multiplier_1_out), .in8(shifter_1_out),
    .in9(shifter_2_out), .in10(shifter_3_out), .in11(shifter_4_out), .in12(negator_1_out),
    .in13(negator_2_out), .in14({16{1'b0}}), .in15({16{1'b0}}), .out(auRESULT), .sel(auSEL));
endmodule

module project_ro (
  input  [15:0] A,
  input  [15:0] B,
  input  [2:0] ruSEL,
  output ruRESULT
);

  wire comparator_1_eq, comparator_1_gt, comparator_1_lt, not_1_out, or_1_out, or_2_out;

  Comparator #(.width(16)) comparator_1 (
    .a(A), .b(B), .gt(comparator_1_gt), .eq(comparator_1_eq), .lt(comparator_1_lt));
  or or_1 (or_1_out, comparator_1_gt, comparator_1_eq);
  or or_2 (or_2_out, comparator_1_lt, comparator_1_eq);
  not not_1 (not_1_out, comparator_1_eq);
  Multiplexer #(.select(3)) multiplexer_1 (
    .in0(comparator_1_gt), .in1(comparator_1_eq), .in2(comparator_1_lt), .in3(or_1_out), .in4(or_2_out),
    .in5(not_1_out), .in6(1'b0), .in7(1'b0), .out(ruRESULT), .sel(ruSEL));
endmodule

module project_alu (
  input  [15:0] A,
  input  [3:0] auSEL,
  input  [15:0] B,
  input  [2:0] ruSEL,
  input  OE,
  output [15:0] aluRESULT,
  output [15:0] aoDOUT,
  output ruRESULT
);

  project_ao project_ao_1 (.A(A), .B(B), .auSEL(auSEL), .auRESULT(aluRESULT));
  project_ro project_ro_1 (.A(A), .B(B), .ruSEL(ruSEL), .ruRESULT(ruRESULT));
  assign aoDOUT = OE ? aluRESULT : 16'bz;  // Controlled_Buffer controlled_buffer_1
endmodule

module Datapath (
  input  WE_MAR,
  input  [15:0] testingData,
  input  oeTestingData,
  input  RESET_MAR,
  input  OE_MAR,
  input  internalOE,
  input  WE_MBR,
  input  WE_IR,
  input  RESET_MBR,
  input  Reset_IR,
  input  OE_IR,
  input  OE_MBR,
  input  WE_A,
  input  WE_OR,
  input  Reset_A,
  input  OE_A,
  input  RESET_OR,
  input  OE_OR,
  input  [3:0] auSel,
  input  [2:0] ruSel,
  input  OE_ALU,
  input  WE_B,
  input  Reset_B,
  input  OE_B,
  output [7:0] marContent,
  output [15:0] irContent,
  output [15:0] mbrContent,
  output [15:0] regAContent,
  output [15:0] DoutA,
  output [15:0] outputContent,
  output ruRes,
  output [15:0] aluResult,
  output [15:0] regBContent,
  output [15:0] DoutB
);

  wire Clk_out;
  wire [7:0] bitselector_1_out, controlled_buffer_6_out;
  wire [15:0] ALU_aodout, controlled_buffer_3_out;

  Clock Clk (.out(Clk_out));
  Register #(.width(16)) instructionRegister (.D(ALU_aodout), .en(WE_IR), .clk(Clk_out), .Q(irContent), .clr(Reset_IR));
  Register #(.width(16)) A (.D(ALU_aodout), .en(WE_A), .clk(Clk_out), .Q(regAContent), .clr(Reset_A));
  Register #(.width(16)) B (.D(ALU_aodout), .en(WE_B), .clk(Clk_out), .Q(regBContent), .clr(Reset_B));
  assign DoutA = OE_A ? regAContent : 16'bz;  // Controlled_Buffer controlled_buffer_1
  assign DoutB = OE_B ? regBContent : 16'bz;  // Controlled_Buffer controlled_buffer_2
  BitSelector #(.group(8), .width(16)) bitselector_1 (.in(irContent), .out(bitselector_1_out), .sel(1'b0));
  assign controlled_buffer_3_out = OE_IR ? irContent : 16'bz;  // Controlled_Buffer controlled_buffer_3
  project_alu ALU (
    .A(regAContent), .auSEL(auSel), .B(regBContent), .ruSEL(ruSel), .OE(OE_ALU), .aluRESULT(aluResult),
    .aoDOUT(ALU_aodout), .ruRESULT(ruRes));
  LED D15 (.in(ALU_aodout[15]));
  LED D14 (.in(ALU_aodout[14]));
  LED D13 (.in(ALU_aodout[13]));
  LED D12 (.in(ALU_aodout[12]));
  LED D11 (.in(ALU_aodout[11]));
  LED D10 (.in(ALU_aodout[10]));
  LED D9 (.in(ALU_aodout[9]));
  LED D8 (.in(ALU_aodout[8]));
  assign ALU_aodout = oeTestingData ? testingData : 16'bz;  // Controlled_Buffer controlled_buffer_4
  LED D6 (.in(ALU_aodout[6]));
  LED D7 (.in(ALU_aodout[7]));
  LED D5 (.in(ALU_aodout[5]));
  LED D4 (.in(ALU_aodout[4]));
  LED D3 (.in(ALU_aodout[3]));
  LED D2 (.in(ALU_aodout[2]));
  LED D1 (.in(ALU_aodout[1]));
  LED D0 (.in(ALU_aodout[0]));
  Register MAR (.D(bitselector_1_out), .en(WE_MAR), .clk(Clk_out), .Q(marContent), .clr(RESET_MAR));
  Register #(.width(16)) MBR (.D(ALU_aodout), .en(WE_MBR), .clk(Clk_out), .Q(mbrContent), .clr(RESET_MBR));
  Register #(.width(16)) outputRegister (.D(ALU_aodout), .en(WE_OR), .clk(Clk_out), .Q(outputContent), .clr(RESET_OR));
  assign ALU_aodout = internalOE ? mbrContent : 16'bz;  // Controlled_Buffer controlled_buffer_5
  assign controlled_buffer_6_out = OE_MAR ? marContent : 8'bz;  // Controlled_Buffer controlled_buffer_6
  assign ALU_aodout = OE_MBR ? mbrContent : 16'bz;  // Controlled_Buffer controlled_buffer_7
  assign ALU_aodout = OE_OR ? outputContent : 16'bz;  // Controlled_Buffer controlled_buffer_8
  LED led_1 (.in(ALU_aodout[15]));
  LED led_2 (.in(ALU_aodout[14]));
  LED led_3 (.in(ALU_aodout[13]));
  LED led_4 (.in(ALU_aodout[12]));
  LED led_5 (.in(ALU_aodout[11]));
  LED led_6 (.in(ALU_aodout[10]));
  LED led_7 (.in(ALU_aodout[9]));
  LED led_8 (.in(ALU_aodout[8]));
  LED led_9 (.in(ALU_aodout[7]));
  LED led_10 (.in(ALU_aodout[6]));
  LED led_11 (.in(ALU_aodout[5]));
  LED led_12 (.in(ALU_aodout[4]));
  LED led_13 (.in(ALU_aodout[3]));
  LED led_14 (.in(ALU_aodout[2]));
  LED led_15 (.in(ALU_aodout[1]));
  LED led_16 (.in(ALU_aodout[0]));
  // also tied to GND on the sheet: {controlled_buffer_3_out[0], controlled_buffer_3_out[1], controlled_buffer_3_out[2], controlled_buffer_3_out[3], controlled_buffer_3_out[4], controlled_buffer_3_out[5], controlled_buffer_3_out[6], controlled_buffer_3_out[7], controlled_buffer_3_out[8], controlled_buffer_3_out[9], controlled_buffer_3_out[10], controlled_buffer_3_out[11], controlled_buffer_3_out[12], controlled_buffer_3_out[13], controlled_buffer_3_out[14], controlled_buffer_3_out[15]}

  // Notes on the sheet:
  //   Internal Address Bus (8 bits)
  //   Internal Data Bus
  //   External Address Bus
  //   Internal Data Bus
endmodule

module CPU (
  input  [15:0] in_1,
  input  OE_TestingData,
  input  reset_mar,
  input  [7:0] content_counter,
  input  result_ir,
  input  Reset_A,
  input  OE_A,
  input  reset_o,
  input  [3:0] auSEL,
  input  [2:0] ruSEL,
  input  Reset_B,
  input  OE_B,
  output [7:0] content_mar,
  output [15:0] Content_IR,
  output [15:0] Content_MBR,
  output [15:0] Dout_IR,
  output [3:0] out_17,
  output [15:0] Content_A,
  output [15:0] Dout_A,
  output [15:0] Content_Output,
  output [2:0] out_21,
  output [15:0] auRESULT,
  output [15:0] Dout,
  output ruRESULT,
  output [15:0] Content_B,
  output [15:0] Dout_B
);

  wire clock_1_out, cu_1_c0, cu_1_c1, cu_1_c2, cu_1_c3, cu_1_c4, cu_1_c5, cu_1_c6, cu_1_c7, cu_1_c8, cu_1_c9,
       cu_1_c10, cu_1_c11, cu_1_c12, cu_1_c13, cu_1_c14, cu_1_c15, undriven;
  wire [7:0] controlled_buffer_1_out, controlled_buffer_7_out;
  wire [15:0] bit_extender_2_out, ram_1_dout;
  wire [31:0] decimal_decoder_1_dout, decimal_decoder_2_dout, decimal_decoder_3_dout, decimal_decoder_4_dout,
       decimal_decoder_5_dout, decimal_decoder_6_dout, decimal_decoder_7_dout;

  Clock clock_1 (.out(clock_1_out));
  Counter programCounter (
    .count(cu_1_c1), .clk(clock_1_out), .D(controlled_buffer_1_out), .Q(content_counter));  // open: clr, load, up, carry
  Register #(.width(16)) Register_B (.D(Dout), .en(cu_1_c13), .clk(clock_1_out), .Q(Content_B), .clr(Reset_B));
  Register #(.width(16)) instructionRegister (
    .D(Dout), .en(cu_1_c7), .clk(clock_1_out), .Q(Content_IR), .clr(result_ir));
  Register #(.width(16)) registerA (.D(Dout), .en(cu_1_c12), .clk(clock_1_out), .Q(Content_A), .clr(Reset_A));
  assign controlled_buffer_1_out = cu_1_c0 ? content_counter : 8'bz;  // Controlled_Buffer controlled_buffer_1
  assign Dout_IR = {{8{content_counter[7]}}, content_counter};  // Bit_Extender bit_extender_1
  assign Dout_IR = cu_1_c8 ? Content_IR : 16'bz;  // Controlled_Buffer controlled_buffer_2
  assign Dout_A = OE_A ? Content_A : 16'bz;  // Controlled_Buffer controlled_buffer_3
  assign Dout_B = OE_B ? Content_B : 16'bz;  // Controlled_Buffer controlled_buffer_4
  BitSelector #(.group(8), .width(16)) bitselector_1 (.in(Dout_IR), .out(controlled_buffer_1_out), .sel(1'b0));
  project_alu project_alu_1 (
    .A(Content_A), .auSEL(auSEL), .B(Content_B), .ruSEL(ruSEL), .OE(cu_1_c11), .aluRESULT(auRESULT),
    .aoDOUT(Dout), .ruRESULT(ruRESULT));
  decimal_decoder decimal_decoder_1 (.Din(Content_IR), .Dout(decimal_decoder_1_dout));
  decimal_decoder decimal_decoder_2 (.Din(Dout_IR), .Dout(decimal_decoder_2_dout));
  decimal_decoder decimal_decoder_3 (.Din(Content_B), .Dout(decimal_decoder_3_dout));
  _7_Segment_Display u_7_segment_display_1 (
    .g(decimal_decoder_2_dout[3]), .f(decimal_decoder_2_dout[2]), .a(decimal_decoder_2_dout[1]),
    .b(decimal_decoder_2_dout[0]), .e(decimal_decoder_2_dout[19]), .d(decimal_decoder_2_dout[18]),
    .c(decimal_decoder_2_dout[17]), .dp(decimal_decoder_2_dout[16]));
  _7_Segment_Display u_7_segment_display_2 (
    .g(decimal_decoder_1_dout[15]), .f(decimal_decoder_1_dout[14]), .a(decimal_decoder_1_dout[13]),
    .b(decimal_decoder_1_dout[12]), .e(decimal_decoder_1_dout[31]), .d(decimal_decoder_1_dout[30]),
    .c(decimal_decoder_1_dout[29]), .dp(decimal_decoder_1_dout[28]));
  _7_Segment_Display u_7_segment_display_3 (
    .g(decimal_decoder_3_dout[15]), .f(decimal_decoder_3_dout[14]), .a(decimal_decoder_3_dout[13]),
    .b(decimal_decoder_3_dout[12]), .e(decimal_decoder_3_dout[31]), .d(decimal_decoder_3_dout[30]),
    .c(decimal_decoder_3_dout[29]), .dp(decimal_decoder_3_dout[28]));
  _7_Segment_Display u_7_segment_display_4 (
    .g(decimal_decoder_1_dout[11]), .f(decimal_decoder_1_dout[10]), .a(decimal_decoder_1_dout[9]),
    .b(decimal_decoder_1_dout[8]), .e(decimal_decoder_1_dout[27]), .d(decimal_decoder_1_dout[26]),
    .c(decimal_decoder_1_dout[25]), .dp(decimal_decoder_1_dout[24]));
  _7_Segment_Display u_7_segment_display_5 (
    .g(decimal_decoder_1_dout[7]), .f(decimal_decoder_1_dout[6]), .a(decimal_decoder_1_dout[5]),
    .b(decimal_decoder_1_dout[4]), .e(decimal_decoder_1_dout[23]), .d(decimal_decoder_1_dout[22]),
    .c(decimal_decoder_1_dout[21]), .dp(decimal_decoder_1_dout[20]));
  decimal_decoder decimal_decoder_4 (.Din(Content_A), .Dout(decimal_decoder_4_dout));
  decimal_decoder decimal_decoder_5 (.Din(auRESULT), .Dout(decimal_decoder_5_dout));
  _7_Segment_Display u_7_segment_display_6 (
    .g(decimal_decoder_3_dout[11]), .f(decimal_decoder_3_dout[10]), .a(decimal_decoder_3_dout[9]),
    .b(decimal_decoder_3_dout[8]), .e(decimal_decoder_3_dout[27]), .d(decimal_decoder_3_dout[26]),
    .c(decimal_decoder_3_dout[25]), .dp(decimal_decoder_3_dout[24]));
  _7_Segment_Display u_7_segment_display_7 (
    .g(decimal_decoder_3_dout[7]), .f(decimal_decoder_3_dout[6]), .a(decimal_decoder_3_dout[5]),
    .b(decimal_decoder_3_dout[4]), .e(decimal_decoder_3_dout[23]), .d(decimal_decoder_3_dout[22]),
    .c(decimal_decoder_3_dout[21]), .dp(decimal_decoder_3_dout[20]));
  _7_Segment_Display u_7_segment_display_8 (
    .g(decimal_decoder_1_dout[3]), .f(decimal_decoder_1_dout[2]), .a(decimal_decoder_1_dout[1]),
    .b(decimal_decoder_1_dout[0]), .e(decimal_decoder_1_dout[19]), .d(decimal_decoder_1_dout[18]),
    .c(decimal_decoder_1_dout[17]), .dp(decimal_decoder_1_dout[16]));
  _7_Segment_Display u_7_segment_display_9 (
    .g(decimal_decoder_4_dout[15]), .f(decimal_decoder_4_dout[14]), .a(decimal_decoder_4_dout[13]),
    .b(decimal_decoder_4_dout[12]), .e(decimal_decoder_4_dout[31]), .d(decimal_decoder_4_dout[30]),
    .c(decimal_decoder_4_dout[29]), .dp(decimal_decoder_4_dout[28]));
  _7_Segment_Display u_7_segment_display_10 (
    .g(decimal_decoder_5_dout[15]), .f(decimal_decoder_5_dout[14]), .a(decimal_decoder_5_dout[13]),
    .b(decimal_decoder_5_dout[12]), .e(decimal_decoder_5_dout[31]), .d(decimal_decoder_5_dout[30]),
    .c(decimal_decoder_5_dout[29]), .dp(decimal_decoder_5_dout[28]));
  _7_Segment_Display u_7_segment_display_11 (
    .g(decimal_decoder_3_dout[3]), .f(decimal_decoder_3_dout[2]), .a(decimal_decoder_3_dout[1]),
    .b(decimal_decoder_3_dout[0]), .e(decimal_decoder_3_dout[19]), .d(decimal_decoder_3_dout[18]),
    .c(decimal_decoder_3_dout[17]), .dp(decimal_decoder_3_dout[16]));
  _7_Segment_Display u_7_segment_display_12 (
    .g(decimal_decoder_4_dout[11]), .f(decimal_decoder_4_dout[10]), .a(decimal_decoder_4_dout[9]),
    .b(decimal_decoder_4_dout[8]), .e(decimal_decoder_4_dout[27]), .d(decimal_decoder_4_dout[26]),
    .c(decimal_decoder_4_dout[25]), .dp(decimal_decoder_4_dout[24]));
  _7_Segment_Display u_7_segment_display_13 (
    .g(decimal_decoder_4_dout[7]), .f(decimal_decoder_4_dout[6]), .a(decimal_decoder_4_dout[5]),
    .b(decimal_decoder_4_dout[4]), .e(decimal_decoder_4_dout[23]), .d(decimal_decoder_4_dout[22]),
    .c(decimal_decoder_4_dout[21]), .dp(decimal_decoder_4_dout[20]));
  _7_Segment_Display u_7_segment_display_14 (
    .g(decimal_decoder_5_dout[11]), .f(decimal_decoder_5_dout[10]), .a(decimal_decoder_5_dout[9]),
    .b(decimal_decoder_5_dout[8]), .e(decimal_decoder_5_dout[27]), .d(decimal_decoder_5_dout[26]),
    .c(decimal_decoder_5_dout[25]), .dp(decimal_decoder_5_dout[24]));
  _7_Segment_Display u_7_segment_display_15 (
    .g(decimal_decoder_5_dout[7]), .f(decimal_decoder_5_dout[6]), .a(decimal_decoder_5_dout[5]),
    .b(decimal_decoder_5_dout[4]), .e(decimal_decoder_5_dout[23]), .d(decimal_decoder_5_dout[22]),
    .c(decimal_decoder_5_dout[21]), .dp(decimal_decoder_5_dout[20]));
  LED D15 (.in(Dout[15]));
  _7_Segment_Display u_7_segment_display_16 (
    .g(decimal_decoder_4_dout[3]), .f(decimal_decoder_4_dout[2]), .a(decimal_decoder_4_dout[1]),
    .b(decimal_decoder_4_dout[0]), .e(decimal_decoder_4_dout[19]), .d(decimal_decoder_4_dout[18]),
    .c(decimal_decoder_4_dout[17]), .dp(decimal_decoder_4_dout[16]));
  _7_Segment_Display u_7_segment_display_17 (
    .g(decimal_decoder_5_dout[3]), .f(decimal_decoder_5_dout[2]), .a(decimal_decoder_5_dout[1]),
    .b(decimal_decoder_5_dout[0]), .e(decimal_decoder_5_dout[19]), .d(decimal_decoder_5_dout[18]),
    .c(decimal_decoder_5_dout[17]), .dp(decimal_decoder_5_dout[16]));
  LED D14 (.in(Dout[14]));
  LED D13 (.in(Dout[13]));
  LED D12 (.in(Dout[12]));
  LED D11 (.in(Dout[11]));
  LED D10 (.in(Dout[10]));
  assign Dout = OE_TestingData ? in_1 : 16'bz;  // Controlled_Buffer controlled_buffer_5
  LED D9 (.in(Dout[9]));
  LED D8 (.in(Dout[8]));
  LED D7 (.in(Dout[7]));
  LED D6 (.in(Dout[6]));
  LED D5 (.in(Dout[5]));
  LED D4 (.in(Dout[4]));
  LED D3 (.in(Dout[3]));
  LED D2 (.in(Dout[2]));
  LED D1 (.in(Dout[1]));
  LED D0 (.in(Dout[0]));
  Register memory_address_register (
    .D(controlled_buffer_1_out), .en(cu_1_c9), .clk(clock_1_out), .Q(content_mar), .clr(reset_mar));
  assign Dout = cu_1_c5 ? Content_MBR : 16'bz;  // Controlled_Buffer controlled_buffer_6
  Register #(.width(16)) memory_buffer_register (
    .D(Dout), .en(cu_1_c4), .clk(clock_1_out), .Q(Content_MBR));  // open: clr
  Register #(.width(16)) Output_Register (
    .D(Dout), .en(cu_1_c15), .clk(clock_1_out), .Q(Content_Output), .clr(reset_o));
  assign controlled_buffer_7_out = cu_1_c10 ? content_mar : 8'bz;  // Controlled_Buffer controlled_buffer_7
  assign Dout = cu_1_c6 ? Content_MBR : 16'bz;  // Controlled_Buffer controlled_buffer_8
  assign Dout = cu_1_c14 ? Content_Output : 16'bz;  // Controlled_Buffer controlled_buffer_9
  decimal_decoder decimal_decoder_6 (.Din(Content_Output), .Dout(decimal_decoder_6_dout));
  _7_Segment_Display u_7_segment_display_18 (
    .g(decimal_decoder_6_dout[15]), .f(decimal_decoder_6_dout[14]), .a(decimal_decoder_6_dout[13]),
    .b(decimal_decoder_6_dout[12]), .e(decimal_decoder_6_dout[31]), .d(decimal_decoder_6_dout[30]),
    .c(decimal_decoder_6_dout[29]), .dp(decimal_decoder_6_dout[28]));
  _7_Segment_Display u_7_segment_display_19 (
    .g(decimal_decoder_6_dout[11]), .f(decimal_decoder_6_dout[10]), .a(decimal_decoder_6_dout[9]),
    .b(decimal_decoder_6_dout[8]), .e(decimal_decoder_6_dout[27]), .d(decimal_decoder_6_dout[26]),
    .c(decimal_decoder_6_dout[25]), .dp(decimal_decoder_6_dout[24]));
  _7_Segment_Display u_7_segment_display_20 (
    .g(decimal_decoder_6_dout[7]), .f(decimal_decoder_6_dout[6]), .a(decimal_decoder_6_dout[5]),
    .b(decimal_decoder_6_dout[4]), .e(decimal_decoder_6_dout[23]), .d(decimal_decoder_6_dout[22]),
    .c(decimal_decoder_6_dout[21]), .dp(decimal_decoder_6_dout[20]));
  _7_Segment_Display u_7_segment_display_21 (
    .g(decimal_decoder_6_dout[3]), .f(decimal_decoder_6_dout[2]), .a(decimal_decoder_6_dout[1]),
    .b(decimal_decoder_6_dout[0]), .e(decimal_decoder_6_dout[19]), .d(decimal_decoder_6_dout[18]),
    .c(decimal_decoder_6_dout[17]), .dp(decimal_decoder_6_dout[16]));
  LED led_1 (.in(Dout[15]));
  LED led_2 (.in(Dout[14]));
  LED led_3 (.in(Dout[13]));
  LED led_4 (.in(Dout[12]));
  LED led_5 (.in(Dout[11]));
  LED led_6 (.in(Dout[10]));
  LED led_7 (.in(Dout[9]));
  LED led_8 (.in(Dout[8]));
  LED led_9 (.in(Dout[7]));
  LED led_10 (.in(Dout[6]));
  LED led_11 (.in(Dout[5]));
  LED led_12 (.in(Dout[4]));
  LED led_13 (.in(Dout[3]));
  LED led_14 (.in(Dout[2]));
  LED led_15 (.in(Dout[1]));
  LED led_16 (.in(Dout[0]));
  RAM #(.dataWidth(16), .enables("line")) ram_1 (
    .addr({controlled_buffer_7_out[0], controlled_buffer_7_out[1], controlled_buffer_7_out[2], controlled_buffer_7_out[3], controlled_buffer_7_out[4], controlled_buffer_7_out[5], controlled_buffer_7_out[6], controlled_buffer_7_out[7]}),
    .we(cu_1_c2), .clk(undriven), .din(Dout), .dout(ram_1_dout));
  assign Dout = cu_1_c3 ? ram_1_dout : 16'bz;  // Controlled_Buffer controlled_buffer_10
  BitSelector #(.group(4), .width(16)) bitselector_2 (.in(Content_IR), .out(out_17), .sel(2'b10));
  Counter #(.max('h7), .width(3)) Step_Counter (.clk(undriven), .Q(out_21));  // open: clr, load, up, count, D, carry
  assign bit_extender_2_out = {{13{out_21[2]}}, out_21};  // Bit_Extender bit_extender_2
  CU cu_1 (
    .OPC3(out_17[0]), .OPC2(out_17[1]), .OPC1(out_17[2]), .OPC0(out_17[3]), .SC2(out_21[0]), .SC1(out_21[1]),
    .SC0(out_21[2]), .C0(cu_1_c0), .C1(cu_1_c1), .C2(cu_1_c2), .C3(cu_1_c3), .C4(cu_1_c4), .C5(cu_1_c5),
    .C6(cu_1_c6), .C7(cu_1_c7), .C8(cu_1_c8), .C9(cu_1_c9), .C10(cu_1_c10), .C11(cu_1_c11), .C12(cu_1_c12),
    .C13(cu_1_c13), .C14(cu_1_c14), .C15(cu_1_c15));
  decimal_decoder decimal_decoder_7 (.Din(bit_extender_2_out), .Dout(decimal_decoder_7_dout));
  _7_Segment_Display u_7_segment_display_22 (
    .g(decimal_decoder_7_dout[3]), .f(decimal_decoder_7_dout[2]), .a(decimal_decoder_7_dout[1]),
    .b(decimal_decoder_7_dout[0]), .e(decimal_decoder_7_dout[19]), .d(decimal_decoder_7_dout[18]),
    .c(decimal_decoder_7_dout[17]), .dp(decimal_decoder_7_dout[16]));

  // Notes on the sheet:
  //   INTERNAL DATA BUS
  //   EXTERNAL DATA BUS (8 bits)
  //   EXTERNAL DATA BUS
endmodule

module decimal_decoder (
  input  [15:0] Din,
  output [31:0] Dout
);

  ROM #(.addrWidth(16), .dataWidth(32)) rom_1 (
    .addr(Din),
    .data({Dout[31:28], Dout[15:12], Dout[27:24], Dout[11:8], Dout[23:20], Dout[7:4], Dout[19:16], Dout[3:0]}));
endmodule

module CU (
  input  OPC3,
  input  OPC2,
  input  OPC1,
  input  OPC0,
  input  SC2,
  input  SC1,
  input  SC0,
  output C0,
  output C1,
  output C2,
  output C3,
  output C4,
  output C5,
  output C6,
  output C7,
  output C8,
  output C9,
  output C10,
  output C11,
  output C12,
  output C13,
  output C14,
  output C15
);

  wire and_4_out, and_5_out, and_6_out, and_7_out, and_8_out, and_9_out, and_10_out, and_13_out, and_14_out,
       and_15_out, and_16_out, and_17_out, and_18_out, and_19_out, and_20_out, not_1_out, not_2_out,
       not_3_out, not_4_out, not_5_out;

  not not_1 (not_1_out, OPC1);
  not not_2 (not_2_out, OPC0);
  not not_3 (not_3_out, SC2);
  not not_4 (not_4_out, SC1);
  not not_5 (not_5_out, SC0);
  and and_1 (C0, not_3_out, not_4_out, not_5_out);
  and and_2 (C1, not_3_out, not_4_out, SC0);
  and and_3 (C2, OPC1, OPC0, SC2, not_4_out, not_5_out);
  and and_4 (and_4_out, not_3_out, not_4_out, SC0);
  and and_5 (and_5_out, not_1_out, SC2, not_4_out, not_5_out);
  and and_6 (and_6_out, not_3_out, not_4_out, SC0);
  and and_7 (and_7_out, not_1_out, SC2, not_4_out, not_5_out);
  and and_8 (and_8_out, OPC1, OPC0, not_3_out, SC0);
  and and_9 (and_9_out, not_3_out, SC1, not_5_out);
  and and_10 (and_10_out, not_1_out, SC2, not_4_out, SC0);
  and and_11 (C6, OPC1, OPC0, SC2, not_4_out, not_5_out);
  and and_12 (C7, not_3_out, SC1, not_5_out);
  and and_13 (and_13_out, not_1_out, not_3_out, SC1, SC0);
  and and_14 (and_14_out, OPC0, not_3_out, SC1, SC0);
  and and_15 (and_15_out, not_3_out, not_4_out, not_5_out);
  and and_16 (and_16_out, not_1_out, not_3_out, SC1, SC0);
  and and_17 (and_17_out, OPC0, not_3_out, SC1, SC0);
  and and_18 (and_18_out, not_3_out, not_4_out, SC0);
  and and_19 (and_19_out, not_1_out, SC2, not_4_out, not_5_out);
  and and_20 (and_20_out, OPC0, SC2, not_4_out, not_5_out);
  and and_21 (C11, OPC1, not_2_out, not_3_out, SC1, SC0);
  and and_22 (C12, not_1_out, not_2_out, SC2, not_4_out, SC0);
  and and_23 (C13, not_1_out, OPC0, SC2, not_4_out, SC0);
  and and_24 (C14, OPC1, OPC0, not_3_out, SC1, SC0);
  and and_25 (C15, OPC1, not_2_out, not_3_out, SC1, SC0);
  or or_1 (C3, and_4_out, and_5_out);
  or or_2 (C4, and_6_out, and_7_out, and_8_out);
  or or_3 (C5, and_9_out, and_10_out);
  or or_4 (C8, and_13_out, and_14_out);
  or or_5 (C9, and_15_out, and_16_out, and_17_out);
  or or_6 (C10, and_18_out, and_19_out, and_20_out);
endmodule
